// Logisim project initial_labs.circ as structural Verilog: 1 circuit, main circuit x3plus6
module x3plus6 (
  input  n1,
  input  n0,
  output O3,
  output O2,
  output O1,
  output O0
);

  wire not_1_out;

  not not_1 (not_1_out, n0);
  or or_1 (O3, n1, n0);
  or or_2 (O2, n1, not_1_out);
  xnor xnor_1 (O1, n1, n0);

  assign O0 = n0;

  // Notes on the sheet:
  //   CLA 1
  //   n
  //   0
  //   1
  //   2
  //   3
  //   Combinational Circuit
  //   n0
  //   n1
  //   0
  //   0
  //   1
  //   0
  //   0
  //   1
  //   1
  //   1
  //   Anlee Nguyen and Garrett Johnson
  //   F(n)
  //   6
  //   9
  //   12
  //   15
  //   O3
  //   O2
  //   0
  //   1
  //   1
  //   0
  //   1
  //   1
  //   1
  //   1
  //   O1
  //   1
  //   0
  //   0
  //   1
  //   O0
  //   0
  //   1
  //   0
  //   1
endmodule
