// Logisim project initial_labs.circ as structural Verilog: 3 circuits, main circuit x3plus6
module x3plus6 (
  input  n1,
  input  n0,
  output O3,
  output O2,
  output O1,
  output O0
);

  wire not_1_out;

  not not_1 (not_1_out, n0);
  or or_1 (O3, n1, n0);
  or or_2 (O2, n1, not_1_out);
  xnor xnor_1 (O1, n1, n0);

  assign O0 = n0;

  // Notes on the sheet:
  //   CLA 1
  //   n
  //   0
  //   1
  //   2
  //   3
  //   Combinational Circuit
  //   n1
  //   n0
  //   0
  //   0
  //   0
  //   1
  //   1
  //   0
  //   1
  //   1
  //   Anlee Nguyen and Garrett Johnson
  //   F(n)
  //   6
  //   9
  //   12
  //   15
  //   O3
  //   O2
  //   0
  //   1
  //   1
  //   0
  //   1
  //   1
  //   1
  //   1
  //   O1
  //   1
  //   0
  //   0
  //   1
  //   O0
  //   0
  //   1
  //   0
  //   1
endmodule

module generator (
  input  [2:0] in_1,
  output [3:0] out_2
);

  wire xor_1_out;

  xor xor_1 (xor_1_out, in_1[0], in_1[1]);
  xor xor_2 (out_2[0], in_1[2], xor_1_out);

  assign out_2[3:1] = in_1;

  // Notes on the sheet:
  //   CLA 2
  //   Anlee Nguyen and Garrett Johnson
  //   completed number with even parity
  //   Parity Generator Circuit: A parity generator that takes a 3 bit number as an input, takes on a parity bit and outputs a 4
endmodule

module \checker  (
  input  [3:0] in_1,
  output out_2
);

  wire xor_1_out, xor_2_out;

  xor xor_1 (xor_1_out, in_1[0], in_1[1]);
  xor xor_2 (xor_2_out, xor_1_out, in_1[2]);
  xor xor_3 (out_2, xor_2_out, in_1[3]);

  // Notes on the sheet:
  //   CLA 2
  //   Anlee Nguyen and Garrett Johnson
  //   Parity Checker Circuit: A checker that will check four bits for even parity. Will output a 1 if the 4 bits do not indicate even parity
endmodule
