// Logisim project RSC.circ as structural Verilog
// AU
module Arith_U (
  input  [31:0] A,
  input  [31:0] B,
  input  [31:0] in_3,
  input  S1,
  input  S0,
  output [31:0] AU_out
);

  wire and_1_out, not_2_out;
  wire [31:0] adder_1_out, multiplexer_1_out, not_1_out;

  assign not_1_out = ~B;  // NOT_Gate not_1, 32 bits wide
  Multiplexer #(.select(2), .width(32)) multiplexer_1 (
    .in0(not_1_out), .in1(B), .in2(in_3), .in3(B), .out(multiplexer_1_out), .sel({S1, S0}));
  not not_2 (not_2_out, S0);
  Adder #(.width(32)) adder_1 (.a(A), .b(multiplexer_1_out), .out(adder_1_out), .cin(not_2_out));  // open: cout
  and and_1 (and_1_out, S1, S0);
  Multiplexer #(.width(32)) multiplexer_2 (.in0(adder_1_out), .in1(multiplexer_1_out), .out(AU_out), .sel(and_1_out));

  // Notes on the sheet:
  //   CLA 4: Arithmetic Unit
  //   Anlee Nguyen and Garrett Johnson
  //   An arithmetic unit ciruit that implements an adder and multiplexers (2x1, 4x1) to use 2 32-bit hexadecimal inputs to output the 32-bit hexadecimal result.
endmodule
