// Logisim project RSC.circ as structural Verilog: 4 circuits, main circuit Arith_U
// AU
module Arith_U (
  input  [31:0] A,
  input  [31:0] B,
  input  S1,
  input  S0,
  output [31:0] AU_out
);

  wire and_1_out, not_2_out;
  wire [31:0] adder_1_out, multiplexer_1_out, not_1_out;

  assign not_1_out = ~B;  // NOT_Gate not_1, 32 bits wide
  Multiplexer #(.select(2), .width(32)) multiplexer_1 (
    .in0(not_1_out), .in1(B), .in2({32{1'b0}}), .in3(B), .out(multiplexer_1_out), .sel({S1, S0}));
  not not_2 (not_2_out, S0);
  Adder #(.width(32)) adder_1 (.a(A), .b(multiplexer_1_out), .out(adder_1_out), .cin(not_2_out));  // open: cout
  and and_1 (and_1_out, S1, S0);
  Multiplexer #(.width(32)) multiplexer_2 (.in0(adder_1_out), .in1(multiplexer_1_out), .out(AU_out), .sel(and_1_out));

  // Notes on the sheet:
  //   CLA 4: Arithmetic Unit
  //   Anlee Nguyen and Garrett Johnson
  //   An arithmetic unit ciruit that implements an adder and multiplexers (2x1, 4x1) to use 2 32-bit hexadecimal inputs to output the 32-bit hexadecimal result.
endmodule

// LU
module Logic_U (
  input  [31:0] A,
  input  [31:0] B,
  input  S1,
  input  S0,
  output [31:0] Logic_Out
);

  wire [31:0] and_1_out, not_1_out, or_1_out, shifter_1_out;

  assign and_1_out = A & B;  // AND_Gate and_1, 32 bits wide
  assign or_1_out = A | B;  // OR_Gate or_1, 32 bits wide
  Shifter #(.shift("ar"), .width(32)) shifter_1 (.in(A), .\dist (5'b00001), .out(shifter_1_out));
  assign not_1_out = ~A;  // NOT_Gate not_1, 32 bits wide
  Multiplexer #(.select(2), .width(32)) multiplexer_1 (
    .in0(and_1_out), .in1(or_1_out), .in2(shifter_1_out), .in3(not_1_out), .out(Logic_Out), .sel({S1, S0}));

  // Notes on the sheet:
  //   CLA: CLA 5
  //   Group 8: Anlee Nguyen and Garrett Johnson
  //   Combination Circuit: Logic Unit Circuit (LU) of RSC 
endmodule

module ALU (
  input  [31:0] A,
  input  [31:0] B,
  input  S2,
  input  S1,
  input  S0,
  output [31:0] ALU_Out
);

  wire [31:0] arith_u_1_au_out, logic_u_1_logic_out;

  Arith_U arith_u_1 (.A(A), .B(B), .S1(S1), .S0(S0), .AU_out(arith_u_1_au_out));
  Logic_U logic_u_1 (.A(A), .B(B), .S1(S1), .S0(S0), .Logic_Out(logic_u_1_logic_out));
  Multiplexer #(.width(32)) multiplexer_1 (.in0(arith_u_1_au_out), .in1(logic_u_1_logic_out), .out(ALU_Out), .sel(S2));

  // Notes on the sheet:
  //   CLA: CLA 5
  //   Group 8: Anlee Nguyen and Garrett Johnson
  //   Combination Circuit: Arithmetic Logic Unit Circuit (ALU) of RSC
endmodule

module SC (
  input  Clock,
  input  Clear,
  output [2:0] SEQ_out
);

  wire [2:0] adder_1_out;

  Adder #(.width(3)) adder_1 (.a(SEQ_out), .b(3'b001), .out(adder_1_out));  // open: cin, cout
  Register #(.width(3)) register_1 (.D(adder_1_out), .en(1'b1), .clk(Clock), .Q(SEQ_out), .clr(Clear));

  // Notes on the sheet:
  //   CLA: CLA 6
  //   Group 8: Anlee Nguyen and Garrett Johnson
  //   Combinational Circuit: Sequence Counter (SC) of RSC
endmodule
