// Logisim project RSC.circ as structural Verilog: 6 circuits, main circuit Arith_U
// AU
module Arith_U (
  input  [31:0] A,
  input  [31:0] B,
  input  S1,
  input  S0,
  output [31:0] AU_out
);

  wire and_1_out, not_2_out;
  wire [31:0] adder_1_out, multiplexer_1_out, not_1_out;

  assign not_1_out = ~B;  // NOT_Gate not_1, 32 bits wide
  Multiplexer #(.select(2), .width(32)) multiplexer_1 (
    .in0(not_1_out), .in1(B), .in2({32{1'b0}}), .in3(B), .out(multiplexer_1_out), .sel({S1, S0}));
  not not_2 (not_2_out, S0);
  Adder #(.width(32)) adder_1 (.a(A), .b(multiplexer_1_out), .out(adder_1_out), .cin(not_2_out));  // open: cout
  and and_1 (and_1_out, S1, S0);
  Multiplexer #(.width(32)) multiplexer_2 (.in0(adder_1_out), .in1(multiplexer_1_out), .out(AU_out), .sel(and_1_out));

  // Notes on the sheet:
  //   CLA 4: Arithmetic Unit
  //   Anlee Nguyen and Garrett Johnson
  //   An arithmetic unit ciruit that implements an adder and multiplexers (2x1, 4x1) to use 2 32-bit hexadecimal inputs to output the 32-bit hexadecimal result.
endmodule

// LU
module Logic_U (
  input  [31:0] A,
  input  [31:0] B,
  input  S1,
  input  S0,
  output [31:0] Logic_Out
);

  wire [31:0] and_1_out, not_1_out, or_1_out, shifter_1_out;

  assign and_1_out = A & B;  // AND_Gate and_1, 32 bits wide
  assign or_1_out = A | B;  // OR_Gate or_1, 32 bits wide
  Shifter #(.shift("ar"), .width(32)) shifter_1 (.in(A), .\dist (5'b00001), .out(shifter_1_out));
  assign not_1_out = ~A;  // NOT_Gate not_1, 32 bits wide
  Multiplexer #(.select(2), .width(32)) multiplexer_1 (
    .in0(and_1_out), .in1(or_1_out), .in2(shifter_1_out), .in3(not_1_out), .out(Logic_Out), .sel({S1, S0}));

  // Notes on the sheet:
  //   CLA: CLA 5
  //   Group 8: Anlee Nguyen and Garrett Johnson
  //   Combination Circuit: Logic Unit Circuit (LU) of RSC 
endmodule

module ALU (
  input  [31:0] A,
  input  [31:0] B,
  input  S2,
  input  S1,
  input  S0,
  output [31:0] ALU_Out
);

  wire [31:0] arith_u_1_au_out, logic_u_1_logic_out;

  Arith_U arith_u_1 (.A(A), .B(B), .S1(S1), .S0(S0), .AU_out(arith_u_1_au_out));
  Logic_U logic_u_1 (.A(A), .B(B), .S1(S1), .S0(S0), .Logic_Out(logic_u_1_logic_out));
  Multiplexer #(.width(32)) multiplexer_1 (.in0(arith_u_1_au_out), .in1(logic_u_1_logic_out), .out(ALU_Out), .sel(S2));

  // Notes on the sheet:
  //   CLA: CLA 5
  //   Group 8: Anlee Nguyen and Garrett Johnson
  //   Combination Circuit: Arithmetic Logic Unit Circuit (ALU) of RSC
endmodule

module SC (
  input  Clock,
  input  Clear,
  output [2:0] SEQ_out
);

  wire [2:0] adder_1_out;

  Adder #(.width(3)) adder_1 (.a(SEQ_out), .b(3'b001), .out(adder_1_out));  // open: cin, cout
  Register #(.width(3)) register_1 (.D(adder_1_out), .en(1'b1), .clk(Clock), .Q(SEQ_out), .clr(Clear));

  // Notes on the sheet:
  //   CLA: CLA 6
  //   Group 8: Anlee Nguyen and Garrett Johnson
  //   Combinational Circuit: Sequence Counter (SC) of RSC
endmodule

module DecoderCircuit (
  input  [31:0] IR_In,
  output [3:0] Debug_Instruction,
  output [15:0] D_Out
);

  wire and_1_out;
  wire [3:0] nor_1_out;

  assign nor_1_out = ~(IR_In[7:4] | IR_In[11:8] | IR_In[15:12] | IR_In[19:16] | IR_In[23:20] | IR_In[27:24] | IR_In[31:28]);  // NOR_Gate nor_1, 4 bits wide
  and and_1 (and_1_out, nor_1_out[0], nor_1_out[1], nor_1_out[2], nor_1_out[3]);
  Decoder #(.select(4)) decoder_1 (
    .out0(D_Out[0]), .out1(D_Out[1]), .out2(D_Out[2]), .out3(D_Out[3]), .out4(D_Out[4]), .out5(D_Out[5]),
    .out6(D_Out[6]), .out7(D_Out[7]), .out8(D_Out[8]), .out9(D_Out[9]), .out10(D_Out[10]), .out11(D_Out[11]),
    .out12(D_Out[12]), .out13(D_Out[13]), .out14(D_Out[14]), .out15(D_Out[15]), .sel(IR_In[3:0]),
    .en(and_1_out));

  assign Debug_Instruction = IR_In[3:0];

  // Notes on the sheet:
  //   CLA: CLA 7
  //   Group 8: Anlee Nguyen and Garrett Johnson
  //   Combinational Circuit: DecoderCircuit of RSC
endmodule

module TimerCircuit (
  input  Clock,
  input  Clear,
  input  Stop,
  output [7:0] T_Out
);

  wire not_1_out;
  wire [2:0] sc_1_seq_out;

  SC sc_1 (.Clock(Clock), .Clear(Clear), .SEQ_out(sc_1_seq_out));
  Decoder #(.select(3)) decoder_1 (
    .out0(T_Out[0]), .out1(T_Out[1]), .out2(T_Out[2]), .out3(T_Out[3]), .out4(T_Out[4]), .out5(T_Out[5]),
    .out6(T_Out[6]), .out7(T_Out[7]), .sel(sc_1_seq_out), .en(not_1_out));
  not not_1 (not_1_out, Stop);

  // Notes on the sheet:
  //   CLA: CLA 7
  //   Group 8: Anlee Nguyen and Garrett Johnson
  //   Combinational Circuit: TimerCircuit of RSC
endmodule
