// Logisim project mod_counter.circ as structural Verilog: 2 circuits, main circuit Display
module Display (
  input  DP
);

  wire clock_1_out, sevensegdecoder_1_a, sevensegdecoder_1_b, sevensegdecoder_1_c, sevensegdecoder_1_d,
       sevensegdecoder_1_dp_out, sevensegdecoder_1_e, sevensegdecoder_1_f, sevensegdecoder_1_g;
  wire [3:0] mod9_1_mod9_output;

  Clock clock_1 (.out(clock_1_out));
  Mod9 mod9_1 (.Clock(clock_1_out), .Mod9_Output(mod9_1_mod9_output));
  SevenSegDecoder sevensegdecoder_1 (
    .DP_In(DP), .BCD_In(mod9_1_mod9_output), .DP_Out(sevensegdecoder_1_dp_out), .a(sevensegdecoder_1_a),
    .b(sevensegdecoder_1_b), .c(sevensegdecoder_1_c), .d(sevensegdecoder_1_d), .e(sevensegdecoder_1_e),
    .f(sevensegdecoder_1_f), .g(sevensegdecoder_1_g));
  _7_Segment_Display u_7_segment_display_1 (
    .g(sevensegdecoder_1_g), .f(sevensegdecoder_1_f), .a(sevensegdecoder_1_a), .b(sevensegdecoder_1_b),
    .e(sevensegdecoder_1_e), .d(sevensegdecoder_1_d), .c(sevensegdecoder_1_c), .dp(sevensegdecoder_1_dp_out));

  // Notes on the sheet:
  //   Garrett Johnson
  //   Seven Segment circuit that displays the values in Mod9 circuit
endmodule

module Mod9 (
  input  Clock,
  output [3:0] Mod9_Output
);

  wire and_1_out, and_2_out, and_3_out, j_k_ff_1_qn, j_k_ff_2_qn, j_k_ff_3_qn, j_k_ff_4_qn, or_1_out;

  and and_1 (and_1_out, j_k_ff_2_qn, Mod9_Output[1], Mod9_Output[0]);
  or or_1 (or_1_out, j_k_ff_3_qn, j_k_ff_4_qn);
  and and_2 (and_2_out, j_k_ff_2_qn, Mod9_Output[0]);
  and and_3 (and_3_out, j_k_ff_2_qn, j_k_ff_1_qn);
  J_K_Flip_Flop j_k_ff_1 (
    .J(and_1_out), .K(1'b1), .clk(Clock), .Q(Mod9_Output[3]), .Qn(j_k_ff_1_qn));  // open: preset, reset
  J_K_Flip_Flop j_k_ff_2 (
    .J(or_1_out), .K(1'b1), .clk(Clock), .Q(Mod9_Output[2]), .Qn(j_k_ff_2_qn));  // open: preset, reset
  J_K_Flip_Flop j_k_ff_3 (
    .J(and_2_out), .K(and_2_out), .clk(Clock), .Q(Mod9_Output[1]), .Qn(j_k_ff_3_qn));  // open: preset, reset
  J_K_Flip_Flop j_k_ff_4 (
    .J(and_3_out), .K(j_k_ff_2_qn), .clk(Clock), .Q(Mod9_Output[0]), .Qn(j_k_ff_4_qn));  // open: preset, reset

  // Notes on the sheet:
  //   Garrett Johnson
  //   Section 001, Date: 10/15/2024, Professor Zhang
  //   OLA 3: (Q(t+5)) MOD 9 circuit with 4 JK Flip Flops
  //   Qa'Qb'
  //   Qb'QcQd
  //   Qc' + Qd'
  //   Qb'Qd
  //   Ja Ka
  //   Jb Kb
  //   Jc Kc
  //   Jd Kd
endmodule
