// Logisim project seven_seg.circ as structural Verilog: 3 circuits, main circuit Display_seg
module Display_seg (
  input  DP,
  input  [3:0] BCD
);

  wire sevensegdecoder_1_a, sevensegdecoder_1_b, sevensegdecoder_1_c, sevensegdecoder_1_d,
       sevensegdecoder_1_dp_out, sevensegdecoder_1_e, sevensegdecoder_1_f, sevensegdecoder_1_g;

  SevenSegDecoder sevensegdecoder_1 (
    .DP_In(DP), .BCD_In(BCD), .DP_Out(sevensegdecoder_1_dp_out), .a(sevensegdecoder_1_a),
    .b(sevensegdecoder_1_b), .c(sevensegdecoder_1_c), .d(sevensegdecoder_1_d), .e(sevensegdecoder_1_e),
    .f(sevensegdecoder_1_f), .g(sevensegdecoder_1_g));
  _7_Segment_Display u_7_segment_display_1 (
    .g(sevensegdecoder_1_g), .f(sevensegdecoder_1_f), .a(sevensegdecoder_1_a), .b(sevensegdecoder_1_b),
    .e(sevensegdecoder_1_e), .d(sevensegdecoder_1_d), .c(sevensegdecoder_1_c), .dp(sevensegdecoder_1_dp_out));

  // Notes on the sheet:
  //   CLA 3
  //   Anlee Nguyen and Garrett Johnson
  //   Seven Segment Display: This circuit displays each hexadecimal from the binary input.
endmodule

module SevenSegDecoder (
  input  DP_In,
  input  [3:0] BCD_In,
  output DP_Out,
  output a,
  output b,
  output c,
  output d,
  output e,
  output f,
  output g
);

  SevenSegPLD sevensegpld_1 (
    .n3(BCD_In[3]), .n2(BCD_In[2]), .n1(BCD_In[1]), .n0(BCD_In[0]), .a(a), .b(b), .c(c), .d(d), .e(e), .f(f),
    .g(g));

  assign DP_Out = DP_In;

  // Notes on the sheet:
  //   CLA 3
  //   Anlee Nguyen and Garrett Johnson
  //   Seven Segment Decoder: This circuit will connect the binary inputs to the designated output labels and the decimal input to the decimal output.
endmodule

module SevenSegPLD (
  input  n3,
  input  n2,
  input  n1,
  input  n0,
  output a,
  output b,
  output c,
  output d,
  output e,
  output f,
  output g
);

  wire and_1_out, and_2_out, and_3_out, and_4_out, and_5_out, and_6_out, and_7_out, and_8_out, and_9_out,
       and_10_out, and_11_out, and_12_out, and_13_out, and_14_out, and_15_out, and_16_out, and_17_out,
       and_18_out, and_19_out, and_20_out, and_21_out, and_22_out, and_23_out, and_24_out, and_25_out,
       and_26_out, and_27_out, and_28_out, and_29_out, and_30_out, and_31_out, and_32_out, and_33_out,
       and_34_out, and_35_out, and_36_out, and_37_out, and_38_out, and_39_out, and_40_out, not_1_out,
       not_2_out, not_3_out, not_4_out;

  not not_1 (not_1_out, n3);
  not not_2 (not_2_out, n2);
  not not_3 (not_3_out, n1);
  not not_4 (not_4_out, n0);
  and and_1 (and_1_out, not_2_out, not_4_out);
  and and_2 (and_2_out, not_1_out, n1);
  and and_3 (and_3_out, not_1_out, n2, n0);
  and and_4 (and_4_out, n3, not_2_out, not_3_out);
  and and_5 (and_5_out, n3, not_4_out);
  and and_6 (and_6_out, n2, n1);
  and and_7 (and_7_out, not_1_out, not_3_out, not_4_out);
  and and_8 (and_8_out, not_1_out, n1, n0);
  and and_9 (and_9_out, not_2_out, not_4_out);
  and and_10 (and_10_out, n3, not_3_out, n0);
  and and_11 (and_11_out, not_1_out, not_2_out);
  and and_12 (and_12_out, not_1_out, n2);
  and and_13 (and_13_out, n3, not_2_out);
  and and_14 (and_14_out, not_3_out, n0);
  and and_15 (and_15_out, not_1_out, not_3_out);
  and and_16 (and_16_out, not_1_out, n0);
  and and_17 (and_17_out, n2, not_3_out, n0);
  and and_18 (and_18_out, not_1_out, not_2_out, not_4_out);
  and and_19 (and_19_out, not_1_out, not_2_out, n1);
  and and_20 (and_20_out, not_1_out, n1, not_4_out);
  and and_21 (and_21_out, not_2_out, not_3_out, not_4_out);
  and and_22 (and_22_out, n3, not_3_out);
  and and_23 (and_23_out, not_2_out, n1, n0);
  and and_24 (and_24_out, n2, n1, not_4_out);
  and and_25 (and_25_out, not_2_out, not_4_out);
  and and_26 (and_26_out, n1, not_4_out);
  and and_27 (and_27_out, n3, n1);
  and and_28 (and_28_out, n3, n2);
  and and_29 (and_29_out, not_3_out, not_4_out);
  and and_30 (and_30_out, not_1_out, n2, not_3_out);
  and and_31 (and_31_out, n2, not_4_out);
  and and_32 (and_32_out, n3, not_2_out);
  and and_33 (and_33_out, n3, n1);
  and and_34 (and_34_out, not_2_out, n1);
  and and_35 (and_35_out, n3, not_2_out);
  and and_36 (and_36_out, not_1_out, n2, not_3_out);
  and and_37 (and_37_out, not_1_out, n2, not_4_out);
  and and_38 (and_38_out, n2, not_3_out, n0);
  and and_39 (and_39_out, n1, not_4_out);
  and and_40 (and_40_out, n3, n0);
  or or_1 (a, and_1_out, and_2_out, and_3_out, and_4_out, and_5_out, and_6_out);
  or or_2 (b, and_7_out, and_8_out, and_9_out, and_10_out, and_11_out);
  or or_3 (c, and_12_out, and_13_out, and_14_out, and_15_out, and_16_out);
  or or_4 (e, and_25_out, and_26_out, and_27_out, and_28_out);
  or or_5 (f, and_29_out, and_30_out, and_31_out, and_32_out, and_33_out);
  or or_6 (g, and_34_out, and_35_out, and_36_out, and_37_out, and_38_out, and_39_out, and_40_out);
  or or_7 (d, and_17_out, and_18_out, and_19_out, and_20_out, and_21_out, and_22_out, and_23_out, and_24_out);

  // Notes on the sheet:
  //   CLA 3
  //   Anlee Nguyen and Garrett Johnson
  //   Seven Segment PLD: This is the circuit for the seven segment truth table we designed. Output displayes 0-F values.
endmodule
