// Logisim project RSC.circ as structural Verilog: 4 circuits, main circuit Arith_U
// AU
module Arith_U (
  input  [31:0] A,
  input  [31:0] B,
  input  S1,
  input  S0,
  output [31:0] AU_out
);

  wire and_1_out, not_2_out;
  wire [31:0] adder_1_out, multiplexer_1_out, not_1_out;

  assign not_1_out = ~B;  // NOT_Gate not_1, 32 bits wide
  Multiplexer #(.select(2), .width(32)) multiplexer_1 (
    .in0(not_1_out), .in1(B), .in2({32{1'b0}}), .in3(B), .out(multiplexer_1_out), .sel({S1, S0}));
  not not_2 (not_2_out, S0);
  Adder #(.width(32)) adder_1 (.a(A), .b(multiplexer_1_out), .out(adder_1_out), .cin(not_2_out));  // open: cout
  and and_1 (and_1_out, S1, S0);
  Multiplexer #(.width(32)) multiplexer_2 (.in0(adder_1_out), .in1(multiplexer_1_out), .out(AU_out), .sel(and_1_out));

  // Notes on the sheet:
  //   CLA 4: Arithmetic Unit
  //   Anlee Nguyen and Garrett Johnson
  //   An arithmetic unit ciruit that implements an adder and multiplexers (2x1, 4x1) to use 2 32-bit hexadecimal inputs to output the 32-bit hexadecimal result.
endmodule

// LU
module Logic_U (
  input  [31:0] A,
  input  [31:0] B,
  input  S1,
  input  S0,
  output [31:0] Logic_Out
);

  wire [31:0] and_1_out, not_1_out, or_1_out, shifter_1_out;

  assign and_1_out = A & B;  // AND_Gate and_1, 32 bits wide
  assign or_1_out = A | B;  // OR_Gate or_1, 32 bits wide
  Shifter #(.shift("ar"), .width(32)) shifter_1 (.in(A), .\dist (5'b00001), .out(shifter_1_out));
  assign not_1_out = ~A;  // NOT_Gate not_1, 32 bits wide
  Multiplexer #(.select(2), .width(32)) multiplexer_1 (
    .in0(and_1_out), .in1(or_1_out), .in2(shifter_1_out), .in3(not_1_out), .out(Logic_Out), .sel({S1, S0}));

  // Notes on the sheet:
  //   CLA: CLA 5
  //   Group 8: Anlee Nguyen and Garrett Johnson
  //   Combination Circuit: Logic Unit Circuit (LU) of RSC 
endmodule

module ALU (
  input  [31:0] A,
  input  [31:0] B,
  input  S2,
  input  S1,
  input  S0,
  output [31:0] ALU_Out
);

  wire [31:0] arith_u_1_au_out, logic_u_1_logic_out;

  Arith_U arith_u_1 (.A(A), .B(B), .S1(S1), .S0(S0), .AU_out(arith_u_1_au_out));
  Logic_U logic_u_1 (.A(A), .B(B), .S1(S1), .S0(S0), .Logic_Out(logic_u_1_logic_out));
  Multiplexer #(.width(32)) multiplexer_1 (.in0(arith_u_1_au_out), .in1(logic_u_1_logic_out), .out(ALU_Out), .sel(S2));

  // Notes on the sheet:
  //   CLA: CLA 5
  //   Group 8: Anlee Nguyen and Garrett Johnson
  //   Combination Circuit: Arithmetic Logic Unit Circuit (ALU) of RSC
endmodule

module RSC (
);

  wire Primary_Clock_out;
  wire [31:0] acc_1_acc_out, alu_1_alu_out, ar_1_ar_out, dr_1_bus_out, dr_1_data_out;

  Clock Primary_Clock (.out(Primary_Clock_out));
  DR dr_1 (
    .DR_Out(dr_1_bus_out), .Clock(Primary_Clock_out), .Data_Out(dr_1_data_out), .Bus_Out(dr_1_bus_out));  // open: Load, Bus_Enable
  R r_1 (.R_In(dr_1_bus_out), .Clock(Primary_Clock_out), .Bus_Out(dr_1_bus_out));  // open: Load, Bus_Enable, R_Out
  ALU alu_1 (.A(acc_1_acc_out), .B(dr_1_bus_out), .ALU_Out(alu_1_alu_out));  // open: S2, S1, S0
  OUTR outr_1 (.OUTR_In(dr_1_bus_out), .Clock(Primary_Clock_out));  // open: Load, OUTR_Out
  AR ar_1 (.AR_In(dr_1_bus_out), .Clock(Primary_Clock_out), .AR_Out(ar_1_ar_out));  // open: Load
  RAM #(.addrWidth(16), .dataWidth(32), .databus("bidir"), .trigger("high")) ram_1 (
    .addr(ar_1_ar_out[15:0]), .data(dr_1_bus_out));  // open: we, oe
  PC pc_1 (
    .PC_In(dr_1_bus_out), .Clock(Primary_Clock_out), .Bus_Out(dr_1_bus_out));  // open: Bus_Enable, Count, Load, PC_Out
  ACC acc_1 (
    .ACC_In(alu_1_alu_out), .Clock(Primary_Clock_out), .ACC_Out(acc_1_acc_out), .Bus_Out(dr_1_bus_out));  // open: Load, Clear, Bus_Enable
  IR ir_1 (.IR_In(dr_1_data_out), .Clock(Primary_Clock_out));  // open: Load, IR_Out

  // Notes on the sheet:
  //   Garrett Johnson
  //   OLA 5: Building a bus circuit with the registers created in OLA 4
endmodule
