// Logisim project PLDs.circ as structural Verilog
// PC_BUS
module PLD_PC_BUS (
  input  t0,
  input  t2,
  output PC_BUS
);

  or or_1 (PC_BUS, t0, t2);

  // Notes on the sheet:
  //   CLA 8: Control Signals
  //   Circuit Name: PLD_PC_BUS
  //   Group 8: Anlee Nguyen and Garrett Johnson
endmodule

// AR_LD
module PLD_AR_LD (
  input  t0,
  input  t2,
  input  t4,
  input  clock,
  input  d1,
  input  d2,
  output AR_LD
);

  wire and_1_out, not_1_out, or_1_out, or_2_out;

  not not_1 (not_1_out, clock);
  or or_1 (or_1_out, d1, d2);
  or or_2 (or_2_out, t0, t2, and_1_out);
  and and_1 (and_1_out, t4, or_1_out);
  and and_2 (AR_LD, or_2_out, not_1_out);

  // Notes on the sheet:
  //   CLA 8: Control Signals
  //   Circuit Name: PLD_AR_LD
  //   Group 8: Anlee Nguyen and Garrett Johnson
endmodule

// PC_LD
module PLD_PC_LD (
  input  t4,
  input  clock,
  input  d5,
  input  d6,
  input  z,
  output PC_LD
);

  wire and_1_out, not_1_out, or_1_out;

  not not_1 (not_1_out, clock);
  or or_1 (or_1_out, d5, and_1_out);
  and and_1 (and_1_out, d6, z);
  and and_2 (PC_LD, t4, or_1_out, not_1_out);

  // Notes on the sheet:
  //   CLA 8: Control Signals
  //   Circuit Name: PLD_PC_LD
  //   Group 8: Anlee Nguyen and Garrett Johnson
endmodule

// PC_INC
module PLD_PC_INC (
  input  t1,
  input  t3,
  input  clock,
  input  d1,
  input  d2,
  input  d6,
  input  z,
  output PC_INC
);

  wire and_1_out, and_2_out, not_1_out, not_2_out, or_1_out, or_2_out;

  not not_1 (not_1_out, clock);
  not not_2 (not_2_out, z);
  and and_1 (and_1_out, d6, not_2_out);
  or or_1 (or_1_out, d1, d2, and_1_out);
  and and_2 (and_2_out, t3, or_1_out);
  or or_2 (or_2_out, t1, and_2_out);
  and and_3 (PC_INC, not_1_out, or_2_out);

  // Notes on the sheet:
  //   CLA 8: Control Signals
  //   Circuit Name: PLD_PC_INC
  //   Group 8: Anlee Nguyen and Garrett Johnson
endmodule

// DR_LD
module PLD_DR_LD (
  input  t1,
  input  t3,
  input  t5,
  input  clock,
  input  d1,
  input  d2,
  input  d5,
  input  d6,
  input  z,
  output DR_LD
);

  wire and_1_out, and_2_out, and_3_out, not_1_out, or_1_out, or_2_out, or_3_out;

  not not_1 (not_1_out, clock);
  or or_1 (or_1_out, d1, d2);
  and and_1 (and_1_out, d6, z);
  and and_2 (and_2_out, t5, or_1_out);
  and and_3 (and_3_out, t3, or_2_out);
  or or_2 (or_2_out, d1, d2, d5, and_1_out);
  or or_3 (or_3_out, t1, and_3_out, and_2_out);
  and and_4 (DR_LD, not_1_out, or_3_out);

  // Notes on the sheet:
  //   CLA 8: Control Signals
  //   Circuit Name: PLD_DR_LD
  //   Group 8: Anlee Nguyen and Garrett Johnson
endmodule

// DR_BUS
module PLD_DR_BUS (
  input  t2,
  input  t4,
  input  t6,
  input  d1,
  input  d2,
  input  d5,
  input  d6,
  input  z,
  output DR_BUS
);

  wire and_1_out, and_2_out, and_3_out, or_1_out, or_2_out;

  or or_1 (or_1_out, d1, d2);
  and and_1 (and_1_out, d6, z);
  and and_2 (and_2_out, t6, or_1_out);
  or or_2 (or_2_out, d1, d2, d5, and_1_out);
  and and_3 (and_3_out, t4, or_2_out);
  or or_3 (DR_BUS, t2, and_3_out, and_2_out);

  // Notes on the sheet:
  //   CLA 8: Control Signals
  //   Circuit Name: PLD_DR_BUS
  //   Group 8: Anlee Nguyen and Garrett Johnson
endmodule

// R_LD
module PLD_R_LD (
  input  t3,
  input  clock,
  input  d3,
  output R_LD
);

  wire not_1_out;

  not not_1 (not_1_out, clock);
  and and_1 (R_LD, t3, not_1_out, d3);

  // Notes on the sheet:
  //   CLA 8: Control Signals
  //   Circuit Name: PLD_R_LD
  //   Group 8: Anlee Nguyen and Garrett Johnson
endmodule

// R_BUS
module PLD_R_BUS (
  input  t3,
  input  d4,
  input  d8,
  input  d9,
  input  d12,
  input  d13,
  output R_BUS
);

  wire or_1_out;

  or or_1 (or_1_out, d4, d8, d9, d12, d13);
  and and_1 (R_BUS, t3, or_1_out);

  // Notes on the sheet:
  //   CLA 8: Control Signals
  //   Circuit Name: PLD_R_BUS
  //   Group 8: Anlee Nguyen and Garrett Johnson
endmodule

// S_LD
module PLD_S_LD (
  input  t3,
  input  clock,
  input  d0,
  output S_LD
);

  wire not_1_out;

  not not_1 (not_1_out, clock);
  and and_1 (S_LD, t3, not_1_out, d0);

  // Notes on the sheet:
  //   CLA 8: Control Signals
  //   Circuit Name: PLD_S_LD
  //   Group 8: Anlee Nguyen and Garrett Johnson
endmodule

// ACC_CLR
module PLD_ACC_CLR (
  input  t3,
  input  d11,
  output ACC_CLR
);

  and and_1 (ACC_CLR, t3, d11);

  // Notes on the sheet:
  //   CLA 8: Control Signals
  //   Circuit Name: PLD_ACC_CLR
  //   Group 8: Anlee Nguyen and Garrett Johnson
endmodule

// ACC_LD
module PLD_ACC_LD (
  input  t3,
  input  t6,
  input  clock,
  input  d1,
  input  d4,
  input  d8,
  input  d9,
  input  d10,
  input  d11,
  input  d12,
  input  d13,
  input  d14,
  input  d15,
  output ACC_LD
);

  wire and_1_out, and_2_out, not_1_out, or_1_out, or_2_out;

  not not_1 (not_1_out, clock);
  or or_1 (or_1_out, d4, d8, d9, d10, d11, d12, d13, d14, d15);
  and and_1 (and_1_out, t3, or_1_out);
  and and_2 (and_2_out, t6, d1);
  or or_2 (or_2_out, and_1_out, and_2_out);
  and and_3 (ACC_LD, or_2_out, not_1_out);

  // Notes on the sheet:
  //   CLA 8: Control Signals
  //   Circuit Name: PLD_ACC_LD
  //   Group 8: Anlee Nguyen and Garrett Johnson
endmodule

// ACC_BUS
module PLD_ACC_BUS (
  input  t3,
  input  t5,
  input  d2,
  input  d3,
  input  d7,
  output ACC_BUS
);

  wire and_1_out, and_2_out, or_1_out;

  or or_1 (or_1_out, d3, d7);
  and and_1 (and_1_out, t3, or_1_out);
  and and_2 (and_2_out, t5, d2);
  or or_2 (ACC_BUS, and_1_out, and_2_out);

  // Notes on the sheet:
  //   CLA 8: Control Signals
  //   Circuit Name: PLD_ACC_BUS
  //   Group 8: Anlee Nguyen and Garrett Johnson
endmodule

// ALU_SEL
module PLD_ALU_SEL (
  input  d1,
  input  d4,
  input  d9,
  input  d10,
  input  d12,
  input  d13,
  input  d14,
  input  d15,
  output S2,
  output S1,
  output S0
);

  or or_1 (S2, d12, d13, d14, d15);
  or or_2 (S1, d1, d4, d10, d14, d15);
  or or_3 (S0, d1, d4, d9, d13, d15);

  // Notes on the sheet:
  //   CLA 8: Control Signals
  //   Circuit Name: PLD_ALU_SEL
  //   Group 8: Anlee Nguyen and Garrett Johnson
endmodule

// Z_LD
module PLD_Z_LD (
  output Z_LD
);


  assign Z_LD = 1'b1;

  // Notes on the sheet:
  //   CLA 8: Control Signals
  //   Circuit Name: PLD_Z_LD
  //   Group 8: Anlee Nguyen and Garrett Johnson
endmodule

// OUTR_LD
module PLD_OUTR_LD (
  input  t3,
  input  clock,
  input  d7,
  output OUTR_LD
);

  wire not_1_out;

  not not_1 (not_1_out, clock);
  and and_1 (OUTR_LD, t3, not_1_out, d7);

  // Notes on the sheet:
  //   CLA 8: Control Signals
  //   Circuit Name: PLD_OUTR_LD
  //   Group 8: Anlee Nguyen and Garrett Johnson
endmodule

// RAM_WE
module PLD_RAM_WE (
  input  t6,
  input  clock,
  input  d2,
  output RAM_WE
);

  wire not_1_out;

  not not_1 (not_1_out, clock);
  and and_1 (RAM_WE, t6, not_1_out, d2);

  // Notes on the sheet:
  //   CLA 8: Control Signals
  //   Circuit Name: PLD_RAM_WE
  //   Group 8: Anlee Nguyen and Garrett Johnson
endmodule

// RAM_OE
module PLD_RAM_OE (
  input  t1,
  input  t3,
  input  t5,
  input  clock,
  input  d1,
  input  d2,
  input  d5,
  input  d6,
  input  z,
  output RAM_WE
);

  wire and_1_out, and_2_out, and_3_out, not_1_out, or_1_out, or_2_out;

  not not_1 (not_1_out, clock);
  or or_1 (or_1_out, d1, d2, d5, and_1_out);
  and and_1 (and_1_out, d6, z);
  and and_2 (and_2_out, t3, or_1_out);
  and and_3 (and_3_out, t5, d1);
  or or_2 (or_2_out, t1, and_2_out, and_3_out);
  and and_4 (RAM_WE, not_1_out, or_2_out);

  // Notes on the sheet:
  //   CLA 8: Control Signals
  //   Circuit Name: PLD_RAM_OE
  //   Group 8: Anlee Nguyen and Garrett Johnson
endmodule

// IR_LD
module PLD_IR_LD (
  input  t2,
  input  clock,
  output IR_LD
);

  wire not_1_out;

  not not_1 (not_1_out, clock);
  and and_1 (IR_LD, t2, not_1_out);

  // Notes on the sheet:
  //   CLA 8: Control Signals
  //   Circuit Name: PLD_IR_LD
  //   Group 8: Anlee Nguyen and Garrett Johnson
endmodule

// SC_CLR
module PLD_SC_CLR (
  input  t4,
  input  t5,
  input  t7,
  input  d1,
  input  d2,
  input  d3,
  input  d4,
  input  d5,
  input  d6,
  input  d7,
  input  d8,
  input  d9,
  input  d10,
  input  d11,
  input  d12,
  input  d13,
  input  d14,
  input  d15,
  input  z,
  output SC_CLR
);

  wire and_1_out, and_2_out, and_3_out, and_4_out, and_5_out, not_1_out, or_1_out, or_2_out, or_3_out;

  not not_1 (not_1_out, z);
  and and_1 (and_1_out, d6, not_1_out);
  and and_2 (and_2_out, d6, z);
  or or_1 (or_1_out, d1, d2);
  or or_2 (or_2_out, d3, d4, and_1_out, d7, d8, d9, d10, d11, d12, d13, d14, d15);
  or or_3 (or_3_out, d5, and_2_out);
  and and_3 (and_3_out, t5, or_3_out);
  and and_4 (and_4_out, t7, or_1_out);
  and and_5 (and_5_out, t4, or_2_out);
  or or_4 (SC_CLR, and_5_out, and_3_out, and_4_out);

  // Notes on the sheet:
  //   CLA 8: Control Signals
  //   Circuit Name: PLD_SC_CLR
  //   Group 8: Anlee Nguyen and Garrett Johnson
endmodule
