// Logisim project RSC.circ as structural Verilog: 10 circuits, main circuit Arith_U
// AU
module Arith_U (
  input  [31:0] A,
  input  [31:0] B,
  input  S1,
  input  S0,
  output [31:0] AU_out
);

  wire and_1_out, not_2_out;
  wire [31:0] adder_1_out, multiplexer_1_out, not_1_out;

  assign not_1_out = ~B;  // NOT_Gate not_1, 32 bits wide
  Multiplexer #(.select(2), .width(32)) multiplexer_1 (
    .in0(not_1_out), .in1(B), .in2({32{1'b0}}), .in3(B), .out(multiplexer_1_out), .sel({S1, S0}));
  not not_2 (not_2_out, S0);
  Adder #(.width(32)) adder_1 (.a(A), .b(multiplexer_1_out), .out(adder_1_out), .cin(not_2_out));  // open: cout
  and and_1 (and_1_out, S1, S0);
  Multiplexer #(.width(32)) multiplexer_2 (.in0(adder_1_out), .in1(multiplexer_1_out), .out(AU_out), .sel(and_1_out));

  // Notes on the sheet:
  //   CLA 4: Arithmetic Unit
  //   Anlee Nguyen and Garrett Johnson
  //   An arithmetic unit ciruit that implements an adder and multiplexers (2x1, 4x1) to use 2 32-bit hexadecimal inputs to output the 32-bit hexadecimal result.
endmodule

// LU
module Logic_U (
  input  [31:0] A,
  input  [31:0] B,
  input  S1,
  input  S0,
  output [31:0] Logic_Out
);

  wire [31:0] and_1_out, not_1_out, or_1_out, shifter_1_out;

  assign and_1_out = A & B;  // AND_Gate and_1, 32 bits wide
  assign or_1_out = A | B;  // OR_Gate or_1, 32 bits wide
  Shifter #(.shift("ar"), .width(32)) shifter_1 (.in(A), .\dist (5'b00001), .out(shifter_1_out));
  assign not_1_out = ~A;  // NOT_Gate not_1, 32 bits wide
  Multiplexer #(.select(2), .width(32)) multiplexer_1 (
    .in0(and_1_out), .in1(or_1_out), .in2(shifter_1_out), .in3(not_1_out), .out(Logic_Out), .sel({S1, S0}));

  // Notes on the sheet:
  //   CLA: CLA 5
  //   Group 8: Anlee Nguyen and Garrett Johnson
  //   Combination Circuit: Logic Unit Circuit (LU) of RSC 
endmodule

module ALU (
  input  [31:0] A,
  input  [31:0] B,
  input  S2,
  input  S1,
  input  S0,
  output [31:0] ALU_Out
);

  wire [31:0] arith_u_1_au_out, logic_u_1_logic_out;

  Arith_U arith_u_1 (.A(A), .B(B), .S1(S1), .S0(S0), .AU_out(arith_u_1_au_out));
  Logic_U logic_u_1 (.A(A), .B(B), .S1(S1), .S0(S0), .Logic_Out(logic_u_1_logic_out));
  Multiplexer #(.width(32)) multiplexer_1 (.in0(arith_u_1_au_out), .in1(logic_u_1_logic_out), .out(ALU_Out), .sel(S2));

  // Notes on the sheet:
  //   CLA: CLA 5
  //   Group 8: Anlee Nguyen and Garrett Johnson
  //   Combination Circuit: Arithmetic Logic Unit Circuit (ALU) of RSC
endmodule

module RSC (
  output [7:0] out_1,
  output [3:0] out_2
);

  wire control_1_acc_bus, control_1_acc_clr, control_1_acc_ld, control_1_ar_ld, control_1_dr_bus,
       control_1_dr_ld, control_1_ir_ld, control_1_outr_ld, control_1_pc_bus, control_1_pc_inc,
       control_1_pc_ld, control_1_r_bus, control_1_r_ld, control_1_ram_oe, control_1_ram_we, control_1_z_ld,
       Primary_Clock_out, z_reg_1_z_out;
  wire [2:0] control_1_alu_s;
  wire [31:0] acc_1_acc_out, alu_1_alu_out, ar_1_ar_out, dr_1_bus_out, dr_1_data_out, ir_1_ir_out,
       outr_1_outr_out;

  Control control_1 (
    .Clock(Primary_Clock_out), .Z_In(z_reg_1_z_out), .IR_In(ir_1_ir_out), .IR_LD(control_1_ir_ld),
    .RAM_WE(control_1_ram_we), .RAM_OE(control_1_ram_oe), .AR_LD(control_1_ar_ld), .PC_LD(control_1_pc_ld),
    .T(out_1), .PC_INC(control_1_pc_inc), .PC_BUS(control_1_pc_bus), .DR_LD(control_1_dr_ld), .D(out_2),
    .DR_BUS(control_1_dr_bus), .R_LD(control_1_r_ld), .R_BUS(control_1_r_bus), .ACC_LD(control_1_acc_ld),
    .ACC_CLR(control_1_acc_clr), .ACC_BUS(control_1_acc_bus), .ALU_S(control_1_alu_s),
    .OUTR_LD(control_1_outr_ld), .Z_LD(control_1_z_ld));
  Clock Primary_Clock (.out(Primary_Clock_out));
  DR dr_1 (
    .DR_Out(dr_1_bus_out), .Load(control_1_dr_ld), .Clock(Primary_Clock_out), .Bus_Enable(control_1_dr_bus),
    .Data_Out(dr_1_data_out), .Bus_Out(dr_1_bus_out));
  R r_1 (
    .R_In(dr_1_bus_out), .Load(control_1_r_ld), .Clock(Primary_Clock_out), .Bus_Enable(control_1_r_bus),
    .Bus_Out(dr_1_bus_out));  // open: R_Out
  Z_Reg z_reg_1 (.Clock(Primary_Clock_out), .Load(control_1_z_ld), .ACC_In(acc_1_acc_out), .Z_Out(z_reg_1_z_out));
  AR ar_1 (.AR_In(dr_1_bus_out), .Load(control_1_ar_ld), .Clock(Primary_Clock_out), .AR_Out(ar_1_ar_out));
  ALU alu_1 (
    .A(acc_1_acc_out), .B(dr_1_bus_out), .S2(control_1_alu_s[2]), .S1(control_1_alu_s[1]),
    .S0(control_1_alu_s[0]), .ALU_Out(alu_1_alu_out));
  OUTR outr_1 (.OUTR_In(dr_1_bus_out), .Load(control_1_outr_ld), .Clock(Primary_Clock_out), .OUTR_Out(outr_1_outr_out));
  Hex_Digit_Display hex_digit_display_1 (.value(outr_1_outr_out[31:28]));  // open: dp
  RAM #(.addrWidth(16), .dataWidth(32), .databus("bidir"), .trigger("high")) ram_1 (
    .addr(ar_1_ar_out[15:0]), .we(control_1_ram_we), .oe(control_1_ram_oe), .data(dr_1_bus_out));
  Hex_Digit_Display hex_digit_display_2 (.value(outr_1_outr_out[23:20]));  // open: dp
  Hex_Digit_Display hex_digit_display_3 (.value(outr_1_outr_out[27:24]));  // open: dp
  Hex_Digit_Display hex_digit_display_4 (.value(outr_1_outr_out[19:16]));  // open: dp
  Hex_Digit_Display hex_digit_display_5 (.value(outr_1_outr_out[15:12]));  // open: dp
  Hex_Digit_Display hex_digit_display_6 (.value(outr_1_outr_out[11:8]));  // open: dp
  PC pc_1 (
    .PC_In(dr_1_bus_out), .Clock(Primary_Clock_out), .Bus_Enable(control_1_pc_bus), .Count(control_1_pc_inc),
    .Load(control_1_pc_ld), .Bus_Out(dr_1_bus_out));  // open: PC_Out
  ACC acc_1 (
    .ACC_In(alu_1_alu_out), .Load(control_1_acc_ld), .Clock(Primary_Clock_out), .Clear(control_1_acc_clr),
    .Bus_Enable(control_1_acc_bus), .ACC_Out(acc_1_acc_out), .Bus_Out(dr_1_bus_out));
  Hex_Digit_Display hex_digit_display_7 (.value(outr_1_outr_out[7:4]));  // open: dp
  Hex_Digit_Display hex_digit_display_8 (.value(outr_1_outr_out[3:0]));  // open: dp
  IR ir_1 (.IR_In(dr_1_data_out), .Load(control_1_ir_ld), .Clock(Primary_Clock_out), .IR_Out(ir_1_ir_out));

  // Notes on the sheet:
  //   Garrett Johnson
  //   RSC Final Project: Building the final circuit that can execute programs
endmodule

module Z_Reg (
  input  Clock,
  input  Load,
  input  [31:0] ACC_In,
  output Z_Out
);

  wire not_1_out, or_1_out;

  or or_1 (or_1_out, ACC_In[0], ACC_In[1], ACC_In[2], ACC_In[3], ACC_In[4], ACC_In[5], ACC_In[6], ACC_In[7], ACC_In[8], ACC_In[9], ACC_In[10], ACC_In[11], ACC_In[12], ACC_In[13], ACC_In[14], ACC_In[15], ACC_In[17], ACC_In[18], ACC_In[19], ACC_In[20], ACC_In[21], ACC_In[22], ACC_In[23], ACC_In[24], ACC_In[25], ACC_In[26], ACC_In[27], ACC_In[28], ACC_In[29], ACC_In[30], ACC_In[31], ACC_In[16]);
  not not_1 (not_1_out, or_1_out);
  Onebit_reg onebit_reg_1 (.Clock(Clock), .Data(not_1_out), .Clear(1'b0), .Load(Load), .Data_Out(Z_Out));

  // Notes on the sheet:
  //   Garrett Johnson
  //   OLA 6: Z Register Circuit
endmodule

module Control (
  input  Clock,
  input  Z_In,
  input  [31:0] IR_In,
  output IR_LD,
  output RAM_WE,
  output RAM_OE,
  output AR_LD,
  output PC_LD,
  output [7:0] T,
  output PC_INC,
  output PC_BUS,
  output DR_LD,
  output [3:0] D,
  output DR_BUS,
  output R_LD,
  output R_BUS,
  output ACC_LD,
  output ACC_CLR,
  output ACC_BUS,
  output [2:0] ALU_S,
  output OUTR_LD,
  output Z_LD
);

  wire pld_s_ld_1_s_ld, pld_sc_clr_1_sc_clr, s_reg_1_data_out;
  wire [15:0] decodercircuit_1_d_out;

  S_reg s_reg_1 (.Clock(Clock), .Data(1'b1), .Clear(1'b0), .Load(pld_s_ld_1_s_ld), .Data_Out(s_reg_1_data_out));
  PLD_S_LD pld_s_ld_1 (.t3(T[3]), .clock(decodercircuit_1_d_out[0]), .d0(Clock), .S_LD(pld_s_ld_1_s_ld));
  TimerCircuit timercircuit_1 (.Clock(Clock), .Clear(pld_sc_clr_1_sc_clr), .Stop(s_reg_1_data_out), .T_Out(T));
  DecoderCircuit decodercircuit_1 (.IR_In(IR_In), .Debug_Instruction(D), .D_Out(decodercircuit_1_d_out));
  PLD_IR_LD pld_ir_ld_1 (.t2(T[2]), .clock(Clock), .IR_LD(IR_LD));
  PLD_RAM_WE pld_ram_we_1 (.t6(T[6]), .clock(Clock), .d2(decodercircuit_1_d_out[2]), .RAM_WE(RAM_WE));
  PLD_RAM_OE pld_ram_oe_1 (
    .t1(T[1]), .t3(T[3]), .t5(T[5]), .clock(Clock), .d1(decodercircuit_1_d_out[1]),
    .d2(decodercircuit_1_d_out[2]), .d5(decodercircuit_1_d_out[5]), .d6(decodercircuit_1_d_out[6]), .z(Z_In),
    .RAM_WE(RAM_OE));
  PLD_AR_LD pld_ar_ld_1 (
    .t0(T[0]), .t2(T[2]), .t4(T[4]), .clock(Clock), .d1(decodercircuit_1_d_out[1]),
    .d2(decodercircuit_1_d_out[2]), .AR_LD(AR_LD));
  PLD_PC_LD pld_pc_ld_1 (
    .t4(T[4]), .clock(Clock), .d5(decodercircuit_1_d_out[5]), .d6(decodercircuit_1_d_out[6]), .z(Z_In),
    .PC_LD(PC_LD));
  PLD_PC_INC pld_pc_inc_1 (
    .t1(T[1]), .t3(T[3]), .clock(Clock), .d1(decodercircuit_1_d_out[1]), .d2(decodercircuit_1_d_out[2]),
    .d6(decodercircuit_1_d_out[6]), .z(Z_In), .PC_INC(PC_INC));
  PLD_PC_BUS pld_pc_bus_1 (.t0(T[0]), .t2(T[2]), .PC_BUS(PC_BUS));
  PLD_DR_LD pld_dr_ld_1 (
    .t1(T[1]), .t3(T[3]), .t5(T[5]), .clock(Clock), .d1(decodercircuit_1_d_out[1]),
    .d2(decodercircuit_1_d_out[2]), .d5(decodercircuit_1_d_out[5]), .d6(decodercircuit_1_d_out[6]), .z(Z_In),
    .DR_LD(DR_LD));
  PLD_DR_BUS pld_dr_bus_1 (
    .t4(T[4]), .t6(T[6]), .d1(decodercircuit_1_d_out[1]), .d2(decodercircuit_1_d_out[2]),
    .d5(decodercircuit_1_d_out[5]), .d6(decodercircuit_1_d_out[6]), .z(Z_In), .DR_BUS(DR_BUS));  // open: t2
  PLD_R_LD pld_r_ld_1 (.t3(T[3]), .clock(Clock), .d3(decodercircuit_1_d_out[3]), .R_LD(R_LD));
  PLD_R_BUS pld_r_bus_1 (
    .t3(T[3]), .d4(decodercircuit_1_d_out[4]), .d8(decodercircuit_1_d_out[8]),
    .d9(decodercircuit_1_d_out[9]), .d12(decodercircuit_1_d_out[12]), .d13(decodercircuit_1_d_out[13]),
    .R_BUS(R_BUS));
  PLD_ACC_LD pld_acc_ld_1 (
    .t3(T[3]), .t6(T[6]), .clock(Clock), .d1(decodercircuit_1_d_out[1]), .d4(decodercircuit_1_d_out[4]),
    .d8(decodercircuit_1_d_out[8]), .d9(decodercircuit_1_d_out[9]), .d10(decodercircuit_1_d_out[10]),
    .d11(decodercircuit_1_d_out[11]), .d12(decodercircuit_1_d_out[12]), .d13(decodercircuit_1_d_out[13]),
    .d14(decodercircuit_1_d_out[14]), .d15(decodercircuit_1_d_out[15]), .ACC_LD(ACC_LD));
  PLD_ACC_CLR pld_acc_clr_1 (.t3(T[3]), .d11(decodercircuit_1_d_out[11]), .ACC_CLR(ACC_CLR));
  PLD_ACC_BUS pld_acc_bus_1 (
    .t3(T[3]), .t5(T[5]), .d2(decodercircuit_1_d_out[2]), .d3(decodercircuit_1_d_out[3]),
    .d7(decodercircuit_1_d_out[7]), .ACC_BUS(ACC_BUS));
  PLD_ALU_SEL pld_alu_sel_1 (
    .d1(decodercircuit_1_d_out[1]), .d4(decodercircuit_1_d_out[4]), .d9(decodercircuit_1_d_out[9]),
    .d10(decodercircuit_1_d_out[10]), .d12(decodercircuit_1_d_out[12]), .d13(decodercircuit_1_d_out[13]),
    .d14(decodercircuit_1_d_out[14]), .d15(decodercircuit_1_d_out[15]), .S2(ALU_S[2]), .S1(ALU_S[1]),
    .S0(ALU_S[0]));
  PLD_OUTR_LD pld_outr_ld_1 (.t3(T[3]), .clock(Clock), .d7(decodercircuit_1_d_out[7]), .OUTR_LD(OUTR_LD));
  PLD_Z_LD pld_z_ld_1 (.Z_LD(Z_LD));
  PLD_SC_CLR pld_sc_clr_1 (
    .t4(T[4]), .t5(T[5]), .t7(T[7]), .d1(decodercircuit_1_d_out[1]), .d2(decodercircuit_1_d_out[2]),
    .d3(decodercircuit_1_d_out[3]), .d4(decodercircuit_1_d_out[4]), .d5(decodercircuit_1_d_out[5]),
    .d6(decodercircuit_1_d_out[6]), .d7(decodercircuit_1_d_out[7]), .d8(decodercircuit_1_d_out[8]),
    .d9(decodercircuit_1_d_out[9]), .d10(decodercircuit_1_d_out[10]), .d11(decodercircuit_1_d_out[11]),
    .d12(decodercircuit_1_d_out[12]), .d13(decodercircuit_1_d_out[13]), .d14(decodercircuit_1_d_out[14]),
    .d15(decodercircuit_1_d_out[15]), .z(Z_In), .SC_CLR(pld_sc_clr_1_sc_clr));

  // Notes on the sheet:
  //   Garrett Johnson
  //   OLA 6: Control Circuit
endmodule

module DecoderCircuit (
  input  [31:0] IR_In,
  output [3:0] Debug_Instruction,
  output [15:0] D_Out
);

  wire and_1_out;
  wire [3:0] nor_1_out;

  assign nor_1_out = ~(IR_In[7:4] | IR_In[11:8] | IR_In[15:12] | IR_In[19:16] | IR_In[23:20] | IR_In[27:24] | IR_In[31:28]);  // NOR_Gate nor_1, 4 bits wide
  and and_1 (and_1_out, nor_1_out[0], nor_1_out[1], nor_1_out[2], nor_1_out[3]);
  Decoder #(.select(4)) decoder_1 (
    .out0(D_Out[0]), .out1(D_Out[1]), .out2(D_Out[2]), .out3(D_Out[3]), .out4(D_Out[4]), .out5(D_Out[5]),
    .out6(D_Out[6]), .out7(D_Out[7]), .out8(D_Out[8]), .out9(D_Out[9]), .out10(D_Out[10]), .out11(D_Out[11]),
    .out12(D_Out[12]), .out13(D_Out[13]), .out14(D_Out[14]), .out15(D_Out[15]), .sel(IR_In[3:0]),
    .en(and_1_out));

  assign Debug_Instruction = IR_In[3:0];

  // Notes on the sheet:
  //   Decoder Circuit
  //   Anlee Nguyen and Garrett Johnson
endmodule

module TimerCircuit (
  input  Clock,
  input  Clear,
  input  Stop,
  output [7:0] T_Out
);

  wire not_1_out;
  wire [2:0] sc_1_seq_out;

  SC sc_1 (.Clock(Clock), .Clear(Clear), .SEQ_out(sc_1_seq_out));
  Decoder #(.select(3)) decoder_1 (
    .out0(T_Out[0]), .out1(T_Out[1]), .out2(T_Out[2]), .out3(T_Out[3]), .out4(T_Out[4]), .out5(T_Out[5]),
    .out6(T_Out[6]), .out7(T_Out[7]), .sel(sc_1_seq_out), .en(not_1_out));
  not not_1 (not_1_out, Stop);

  // Notes on the sheet:
  //   Timer Circuit
  //   Anlee  Nguyen and Garrett Johnson
endmodule

module SC (
  input  Clock,
  input  Clear,
  output [2:0] SEQ_out
);

  wire [2:0] adder_1_out;

  Adder #(.width(3)) adder_1 (.a(SEQ_out), .b(3'b001), .out(adder_1_out));  // open: cin, cout
  Register #(.width(3)) register_1 (.D(adder_1_out), .en(1'b1), .clk(Clock), .Q(SEQ_out), .clr(Clear));

  // Notes on the sheet:
  //   Garrett Johnson
  //   SC Circuit
endmodule

module S_reg (
  input  Clock,
  input  Data,
  input  Clear,
  input  Load,
  output Data_Out
);

  wire and_1_out, and_2_out, not_1_out;

  and and_1 (and_1_out, Data, Load);
  not not_1 (not_1_out, Data);
  and and_2 (and_2_out, not_1_out, Load);
  J_K_Flip_Flop j_k_ff_1 (
    .J(and_1_out), .K(and_2_out), .clk(Clock), .Q(Data_Out), .preset(1'b0), .reset(Clear));  // open: Qn

  // Notes on the sheet:
  //   Garrett Johnson
  //   S register circuit
endmodule
