// Logisim project custom_reg_ola4.circ as structural Verilog: 12 circuits, main circuit Onebit_reg
module Onebit_reg (
  input  Clock,
  input  Data,
  input  Clear,
  input  Load,
  output Data_Out
);

  wire and_1_out, and_2_out, not_1_out;

  and and_1 (and_1_out, Data, Load);
  not not_1 (not_1_out, Data);
  and and_2 (and_2_out, not_1_out, Load);
  J_K_Flip_Flop j_k_ff_1 (
    .J(and_1_out), .K(and_2_out), .clk(Clock), .Q(Data_Out), .preset(1'b0), .reset(Clear));  // open: Qn

  // Notes on the sheet:
  //   One bit Register
endmodule

module BasicRegister (
  input  [31:0] Data_In,
  input  Load,
  input  Clock,
  output [31:0] Data_Out
);

  Register #(.width(32)) register_1 (.D(Data_In), .en(Load), .clk(Clock), .Q(Data_Out));  // open: clr

  // Notes on the sheet:
  //   BasicRegister
  //   Garrett Johnson
  //   OLA 4: Designing Register Circuits for loading binary numbers and doing operations
endmodule

module BusRegister (
  input  [31:0] Data_In,
  input  Load,
  input  Clock,
  input  Bus_Enable,
  output [31:0] Data_Out,
  output [31:0] Bus_Out
);

  Register #(.width(32)) register_1 (.D(Data_In), .en(Load), .clk(Clock), .Q(Data_Out));  // open: clr
  assign Bus_Out = Bus_Enable ? Data_Out : 32'bz;  // Controlled_Buffer controlled_buffer_1

  // Notes on the sheet:
  //   Garrett Johnson
  //   BusRegister
endmodule

module ClearRegister (
  input  [31:0] Data_In,
  input  Load,
  input  Clock,
  input  Clear,
  input  Bus_Enable,
  output [31:0] Data_Out,
  output [31:0] Bus_Out
);

  Register #(.width(32)) register_1 (.D(Data_In), .en(Load), .clk(Clock), .Q(Data_Out), .clr(Clear));
  assign Bus_Out = Bus_Enable ? Data_Out : 32'bz;  // Controlled_Buffer controlled_buffer_1

  // Notes on the sheet:
  //   Garrett Johnson
  //   ClearRegister
endmodule

module CountRegister (
  input  [31:0] Data_In,
  input  Clock,
  input  Bus_Enable,
  input  Count,
  input  Load,
  output [31:0] Data_Out,
  output [31:0] Bus_Out
);

  wire or_1_out;
  wire [31:0] adder_1_out, multiplexer_1_out;

  Adder #(.width(32)) adder_1 (.a(Data_Out), .b(32'h1), .out(adder_1_out));  // open: cin, cout
  Multiplexer #(.width(32)) multiplexer_1 (.in0(Data_In), .in1(adder_1_out), .out(multiplexer_1_out), .sel(Count));
  or or_1 (or_1_out, Count, Load);
  Register #(.width(32)) register_1 (.D(multiplexer_1_out), .en(or_1_out), .clk(Clock), .Q(Data_Out));  // open: clr
  assign Bus_Out = Bus_Enable ? Data_Out : 32'bz;  // Controlled_Buffer controlled_buffer_1

  // Notes on the sheet:
  //   CountRegister
  //   Garrett Johnson
endmodule

module ACC (
  input  [31:0] ACC_In,
  input  Load,
  input  Clock,
  input  Clear,
  input  Bus_Enable,
  output [31:0] ACC_Out,
  output [31:0] Bus_Out
);

  ClearRegister clearregister_1 (
    .Data_In(ACC_In), .Load(Load), .Clock(Clock), .Clear(Clear), .Bus_Enable(Bus_Enable), .Data_Out(ACC_Out),
    .Bus_Out(Bus_Out));

  // Notes on the sheet:
  //   ACC
endmodule

module AR (
  input  [31:0] AR_In,
  input  Load,
  input  Clock,
  output [31:0] AR_Out
);

  BasicRegister basicregister_1 (.Data_In(AR_In), .Load(Load), .Clock(Clock), .Data_Out(AR_Out));

  // Notes on the sheet:
  //   AR
endmodule

module DR (
  input  [31:0] DR_Out,
  input  Load,
  input  Clock,
  input  Bus_Enable,
  output [31:0] Data_Out,
  output [31:0] Bus_Out
);

  BusRegister busregister_1 (
    .Data_In(DR_Out), .Load(Load), .Clock(Clock), .Bus_Enable(Bus_Enable), .Data_Out(Data_Out),
    .Bus_Out(Bus_Out));

  // Notes on the sheet:
  //   DR
endmodule

module IR (
  input  [31:0] IR_In,
  input  Load,
  input  Clock,
  output [31:0] IR_Out
);

  BasicRegister basicregister_1 (.Data_In(IR_In), .Load(Load), .Clock(Clock), .Data_Out(IR_Out));

  // Notes on the sheet:
  //   IR
endmodule

module OUTR (
  input  [31:0] OUTR_In,
  input  Load,
  input  Clock,
  output [31:0] OUTR_Out
);

  BasicRegister basicregister_1 (.Data_In(OUTR_In), .Load(Load), .Clock(Clock), .Data_Out(OUTR_Out));

  // Notes on the sheet:
  //   OUTR
endmodule

module PC (
  input  [31:0] PC_In,
  input  Clock,
  input  Bus_Enable,
  input  Count,
  input  Load,
  output [31:0] PC_Out,
  output [31:0] Bus_Out
);

  CountRegister countregister_1 (
    .Data_In(PC_In), .Clock(Clock), .Bus_Enable(Bus_Enable), .Count(Count), .Load(Load), .Data_Out(PC_Out),
    .Bus_Out(Bus_Out));

  // Notes on the sheet:
  //   PC
endmodule

module R (
  input  [31:0] R_In,
  input  Load,
  input  Clock,
  input  Bus_Enable,
  output [31:0] R_Out,
  output [31:0] Bus_Out
);

  BusRegister busregister_1 (
    .Data_In(R_In), .Load(Load), .Clock(Clock), .Bus_Enable(Bus_Enable), .Data_Out(R_Out), .Bus_Out(Bus_Out));

  // Notes on the sheet:
  //   R
endmodule
